# Fritzing sketch Basis-Variante (saved by Fritzing 0.9.2b)

parts:
  Bauteil1 = Arduino Uno (Rev3)  # not connected
  Bauteil2 = Arduino Motor Shield (Rev3)
  M1 = DC Motor
  M2 = DC Motor
  VCC1 = 4 x AAA Battery Mount
  J1 = Infrared Proximity Sensor
  J2 = Basic Servo

nets:
  GND: Bauteil2.GND, VCC1.-, J1.GND, J2.gnd
  N1: Bauteil2.A3, J1.Vout
  VCC: Bauteil2.5V, J1.Vcc, J2.vcc
  N2: Bauteil2.B-, M1.pin_2
  N3: Bauteil2.B+, M1.pin_1
  N4: Bauteil2.A-, M2.pin_2
  N5: Bauteil2.A+, M2.pin_1
  N6: Bauteil2.VMOT, VCC1.+
  N7: Bauteil2.D5_PWM, J2.pulse
