# Fritzing sketch Bluetooth-Erweiterung-Uno (saved by Fritzing 0.9.2b)

parts:
  BLUEFRUIT1 = Adafruit Bluefruit EZ-LINK v1.0
  Bauteil1 = Arduino Uno (Rev3)
  C1 = Ceramic Capacitor [capacitance=100nF package="100 mil [THT, multilayer]"]

nets:
  GND: BLUEFRUIT1.GND, Bauteil1.GND
  VIN: BLUEFRUIT1.Vin, Bauteil1.5V
  N1: BLUEFRUIT1.TX, Bauteil1.D0/RX
  N2: BLUEFRUIT1.RX, Bauteil1.D1/TX
  N3: BLUEFRUIT1.DTR, C1.0
  N4: Bauteil1.RESET, C1.1

custom parts:
  Adafruit Bluefruit EZ-LINK v1.0: Bluefruit EZ-LINK, Bluetooth Serial Link & Arduino Programmer
