# Fritzing sketch Bluetooth-Erweiterung (saved by Fritzing 0.9.2b)

parts:
  Bauteil1 = Arduino Pro
  BLUEFRUIT1 = Adafruit Bluefruit EZ-LINK v1.0

nets:
  N1: Bauteil1.DTR, BLUEFRUIT1.DTR
  N2: Bauteil1.TX, BLUEFRUIT1.RX
  N3: Bauteil1.RX, BLUEFRUIT1.TX
  3V3: Bauteil1.3V3, BLUEFRUIT1.Vin
  GND: Bauteil1.GND, BLUEFRUIT1.GND, BLUEFRUIT1.DSR

custom parts:
  Adafruit Bluefruit EZ-LINK v1.0: Bluefruit EZ-LINK, Bluetooth Serial Link & Arduino Programmer
