# Fritzing sketch HC-SR04-Erweiterung (saved by Fritzing 0.9.2b)

parts:
  Bauteil1 = Arduino Uno (Rev3)  # not connected
  Bauteil2 = Arduino Motor Shield (Rev3)
  M1 = DC Motor
  M2 = DC Motor
  VCC1 = 4 x AAA Battery Mount
  Ultrasonic_sensor1 = HC-SR04
  J1 = Basic Servo

nets:
  N1: Bauteil2.D6_PWM, Ultrasonic_sensor1.Echo
  N2: Bauteil2.D7, Ultrasonic_sensor1.Trig
  N3: Bauteil2.B-, M1.pin_2
  N4: Bauteil2.B+, M1.pin_1
  N5: Bauteil2.A-, M2.pin_2
  N6: Bauteil2.A+, M2.pin_1
  N7: Bauteil2.VMOT, VCC1.+
  GND: Bauteil2.GND, VCC1.-, Ultrasonic_sensor1.GND, J1.gnd
  N8: Bauteil2.D5_PWM, J1.pulse
  VCC: Bauteil2.5V, Ultrasonic_sensor1.VCC, J1.vcc
